# Fritzing sketch Main Circuit Diagram (saved by Fritzing 0.8.7b)

parts:
  Part1 = Arduino Pro Mini v13
  U1 = Mini-360 DC-DC Buck converter [package=THT]
  Part2 = RFID-RC522-v2
  LED1 = LEDs [package=led10mm]
  J1 = Piezo Speaker
  M1 = DC Motor
  R1 = Resistor [tolerance=±5% resistance=220 package=THT]
  BAT1 = BC9VPC [package=bc9vpc]
  U2 = SWITCH_SPDT [package=kps-1290]

nets:
  N1: Part1.VCC, U1.OUT+, Part2.3_3V
  GND: Part1.GND, U1.OUT-, Part2.GND, J1.pin1, M1.pin_2, R1.Pin_0
  N2: Part1.D13/SCK, Part2.SCK
  N3: Part1.D12/MISO, Part2.MISO
  N4: Part1.D11_PWM/MOSI, Part2.MOSI
  N5: Part1.D10_PWM/SS, Part2.SDA
  N6: Part1.D9_PWM, Part2.RST
  N7: Part1.D7, LED1.C, M1.pin_1
  N8: Part1.D4, J1.pin2
  N9: U1.IN-, BAT1.V+
  N10: U1.IN+, U2.P
  N11: LED1.A, R1.Pin_1
  N12: BAT1.V-, U2.O

custom parts:
  Mini-360 DC-DC Buck converter: Mini-360 DC-DC Buck converter. Tiny buck step down voltage converter, input voltage 4.75 to 23V output 1 to 17V adjustable. Available from ebay and the like.
  RFID-RC522-v2: A simple China made RFID-RC522 Reader; do check the pin labels, as this is a MFRC522 based clone.
